// Logisim project lab11.circ as structural Verilog: 1 circuit, main circuit main
module main (
  input  GO,
  input  ESTOP,
  input  DIRECTION,
  input  TOP,
  input  BOTTOM,
  output MOTOR_DOWN,
  output MOTOR_UP
);

  wire and_1_out, and_2_out, and_3_out, or_1_out;

  or or_1 (or_1_out, and_1_out, GO);
  and and_1 (and_1_out, or_1_out, ~ESTOP);  // AND_Gate
  and and_2 (and_2_out, and_1_out, DIRECTION);
  and and_3 (and_3_out, and_1_out, ~DIRECTION);  // AND_Gate
  and and_4 (MOTOR_DOWN, ~BOTTOM, and_2_out);  // AND_Gate
  and and_5 (MOTOR_UP, and_3_out, ~TOP);  // AND_Gate
endmodule
