// Logisim project lab4a-2.circ as structural Verilog: 9 circuits, main circuit main
module main (
  input  WL4,
  input  WL3,
  input  WL2,
  input  WL1
);

  wire circ0_1_out_5, circ1_1_out, circ2_1_out, circ3_1_out, circ4_1_out, circ5_1_out_5, circ6_1_out;

  circ0 circ0_1 (.lv1(WL1), .lv2(WL2), .lv3(WL3), .lv4(WL4), .out_5(circ0_1_out_5));
  circ1 circ1_1 (.lv1(WL1), .lv2(WL2), .lv3(WL3), .lv4(WL4), .out(circ1_1_out));
  circ2 circ2_1 (.lv1(WL1), .lv2(WL2), .lv3(WL3), .lv4(WL4), .out(circ2_1_out));
  circ3 circ3_1 (.lv1(WL1), .lv2(WL2), .lv3(WL3), .lv4(WL4), .out(circ3_1_out));
  circ4 circ4_1 (.lv1(WL1), .lv2(WL2), .lv3(WL3), .lv4(WL4), .out(circ4_1_out));
  circ5 circ5_1 (.lv1(WL1), .lv2(WL2), .lv3(WL3), .lv4(WL4), .out_5(circ5_1_out_5));
  circ6 circ6_1 (.lv1(WL1), .lv2(WL2), .lv3(WL3), .lv4(WL4), .out(circ6_1_out));
  _7_Segment_Display u_7_segment_display_1 (
    .g(circ0_1_out_5), .f(circ1_1_out), .a(circ2_1_out), .b(circ3_1_out), .e(circ4_1_out), .d(circ5_1_out_5),
    .c(circ6_1_out));  // open: dp
endmodule

module circ0 (
  input  lv1,
  input  lv2,
  input  lv3,
  input  lv4,
  output out_5
);

  wire and_1_out, and_2_out, and_3_out, circerror_1_out;

  and and_1 (and_1_out, lv1, lv2, ~lv3, ~lv4);  // AND_Gate
  and and_2 (and_2_out, lv1, lv2, lv3, ~lv4);  // AND_Gate
  and and_3 (and_3_out, lv1, lv2, lv3, lv4);
  circError circerror_1 (.lv1(lv1), .lv2(lv2), .lv3(lv3), .lv4(lv4), .out(circerror_1_out));
  or or_1 (out_5, and_1_out, and_2_out, and_3_out, circerror_1_out);
endmodule

module circ1 (
  input  lv1,
  input  lv2,
  input  lv3,
  input  lv4,
  output out
);

  wire and_1_out, and_2_out, circerror_1_out;

  and and_1 (and_1_out, ~lv1, ~lv2, ~lv3, ~lv4);  // AND_Gate
  and and_2 (and_2_out, lv1, lv2, lv3, lv4);
  circError circerror_1 (.lv1(lv1), .lv2(lv2), .lv3(lv3), .lv4(lv4), .out(circerror_1_out));
  or or_1 (out, and_1_out, and_2_out, circerror_1_out);
endmodule

module circ2 (
  input  lv1,
  input  lv2,
  input  lv3,
  input  lv4,
  output out
);

  wire and_1_out, and_2_out, and_3_out, circerror_1_out;

  and and_1 (and_1_out, ~lv1, ~lv2, ~lv3, ~lv4);  // AND_Gate
  and and_2 (and_2_out, lv1, lv2, ~lv3, ~lv4);  // AND_Gate
  and and_3 (and_3_out, lv1, lv2, lv3, ~lv4);  // AND_Gate
  circError circerror_1 (.lv1(lv1), .lv2(lv2), .lv3(lv3), .lv4(lv4), .out(circerror_1_out));
  or or_1 (out, and_1_out, and_2_out, and_3_out, circerror_1_out);
endmodule

module circ3 (
  input  lv1,
  input  lv2,
  input  lv3,
  input  lv4,
  output out
);

  wire and_1_out, and_2_out, and_3_out, and_4_out, and_5_out;

  and and_1 (and_1_out, ~lv1, ~lv2, ~lv3, ~lv4);  // AND_Gate
  and and_2 (and_2_out, lv1, ~lv2, ~lv3, ~lv4);  // AND_Gate
  and and_3 (and_3_out, lv1, lv2, ~lv3, ~lv4);  // AND_Gate
  and and_4 (and_4_out, lv1, lv2, lv3, ~lv4);  // AND_Gate
  and and_5 (and_5_out, lv1, lv2, lv3, lv4);
  or or_1 (out, and_1_out, and_2_out, and_3_out, and_4_out, and_5_out);
endmodule

module circ4 (
  input  lv1,
  input  lv2,
  input  lv3,
  input  lv4,
  output out
);

  wire and_1_out, and_2_out, circerror_1_out;

  and and_1 (and_1_out, ~lv1, ~lv2, ~lv3, ~lv4);  // AND_Gate
  and and_2 (and_2_out, lv1, lv2, ~lv3, ~lv4);  // AND_Gate
  circError circerror_1 (.lv1(lv1), .lv2(lv2), .lv3(lv3), .lv4(lv4), .out(circerror_1_out));
  or or_1 (out, and_1_out, and_2_out, circerror_1_out);
endmodule

module circ5 (
  input  lv1,
  input  lv2,
  input  lv3,
  input  lv4,
  output out_5
);

  wire and_1_out, and_2_out, and_3_out, circerror_1_out;

  circError circerror_1 (.lv1(lv1), .lv2(lv2), .lv3(lv3), .lv4(lv4), .out(circerror_1_out));
  and and_1 (and_1_out, ~lv1, ~lv2, ~lv3, ~lv4);  // AND_Gate
  and and_2 (and_2_out, lv1, lv2, ~lv3, ~lv4);  // AND_Gate
  and and_3 (and_3_out, lv1, lv2, lv3, ~lv4);  // AND_Gate
  or or_1 (out_5, and_1_out, and_2_out, and_3_out, circerror_1_out);
endmodule

module circ6 (
  input  lv1,
  input  lv2,
  input  lv3,
  input  lv4,
  output out
);

  wire and_1_out, and_2_out, and_3_out, and_4_out;

  and and_1 (and_1_out, ~lv1, ~lv2, ~lv3, ~lv4);  // AND_Gate
  and and_2 (and_2_out, lv1, ~lv2, ~lv3, ~lv4);  // AND_Gate
  and and_3 (and_3_out, lv1, lv2, lv3, ~lv4);  // AND_Gate
  and and_4 (and_4_out, lv1, lv2, lv3, lv4);
  or or_1 (out, and_1_out, and_2_out, and_3_out, and_4_out);
endmodule

module circError (
  input  lv1,
  input  lv2,
  input  lv3,
  input  lv4,
  output out
);

  wire and_1_out, and_2_out, and_3_out;

  and and_1 (and_1_out, ~lv1, lv2);  // AND_Gate
  and and_2 (and_2_out, ~lv2, lv3);  // AND_Gate
  and and_3 (and_3_out, ~lv3, lv4);  // AND_Gate
  or or_1 (out, and_1_out, and_2_out, and_3_out);
endmodule
